// Logisim project tP2_1.circ as structural Verilog: 1 circuit, main circuit main
module main (
  input  A,
  input  EN_A,
  input  B,
  input  EN_B,
  input  Cin,
  input  F0,
  input  F1,
  output out_8,
  output out_9
);

  wire _1_2_out, _1_out, and_1_out, and_2_out, and_3_out, and_4_out, and_5_out, and_6_out, and_7_out,
       and_8_out, and_9_out, and_10_out, and_11_out, and_12_out, and_13_out, ET_out, not_1_out, not_2_out,
       not_3_out, not_4_out, not_5_out, not_6_out, or_1_out, or_2_out, xor_1_out, xor_2_out, xor_3_out;

  and and_1 (and_1_out, A, EN_A);
  and and_2 (and_2_out, B, EN_B);
  not not_1 (not_1_out, F0);
  not not_2 (not_2_out, F0);
  not not_3 (not_3_out, F1);
  and and_3 (and_3_out, not_1_out, and_1_out, not_3_out);
  and and_4 (and_4_out, not_1_out, and_2_out, not_3_out);
  and and_5 (and_5_out, not_1_out, Cin, not_3_out);
  and and_6 (and_6_out, not_2_out, and_1_out, F1);
  and and_7 (and_7_out, not_2_out, and_2_out, F1);
  and and_8 (and_8_out, not_2_out, Cin, F1);
  xor _1 (_1_out, and_3_out, and_4_out);
  not not_4 (not_4_out, and_6_out);
  not not_5 (not_5_out, and_1_out);
  and ET (ET_out, and_1_out, and_2_out);
  not not_6 (not_6_out, F1);
  xor xor_1 (xor_1_out, and_6_out, and_7_out);
  and and_9 (and_9_out, ET_out, F0, not_6_out);
  xor xor_2 (xor_2_out, _1_out, and_5_out);
  and and_10 (and_10_out, and_5_out, _1_out);
  and and_11 (and_11_out, and_3_out, and_4_out);
  or or_1 (or_1_out, and_8_out, and_7_out);
  and and_12 (and_12_out, F0, not_5_out, F1);
  or _1_2 (_1_2_out, and_10_out, and_11_out);
  xor xor_3 (xor_3_out, xor_1_out, and_8_out);
  and and_13 (and_13_out, or_1_out, not_4_out);
  or or_2 (or_2_out, and_8_out, and_7_out, and_13_out);
  or or_3 (out_8, xor_2_out, xor_3_out, and_12_out, and_9_out);
  or or_4 (out_9, _1_2_out, or_2_out);

  // Notes on the sheet:
  //   ADDITIONNEUR
  //   SOUSTRACTEUR
  //   NON(A)
endmodule
