// Logisim project tP2_2.circ as structural Verilog: 1 circuit, main circuit main
module main (
  input  Cin,
  input  A,
  input  EN_A,
  input  E,
  input  EN_E,
  input  B,
  input  EN_B,
  input  F,
  input  EN_F,
  input  C,
  input  EN_C,
  input  G,
  input  EN_G,
  input  D,
  input  EN_D,
  input  H,
  input  EN_H,
  input  F0,
  input  F1,
  output out_20,
  output out_21,
  output out_22,
  output out_23,
  output Cout
);

  wire _1_2_out, _1_3_out, _1_4_out, _1_5_out, _1_6_out, _1_7_out, _1_8_out, _1_out, and_1_out, and_2_out,
       and_3_out, and_4_out, and_5_out, and_6_out, and_7_out, and_8_out, and_9_out, and_10_out, and_11_out,
       and_12_out, and_13_out, and_14_out, and_15_out, and_16_out, and_17_out, and_18_out, and_19_out,
       and_20_out, and_21_out, and_22_out, and_23_out, and_24_out, and_25_out, and_26_out, and_27_out,
       and_28_out, and_29_out, and_30_out, and_31_out, and_32_out, and_33_out, and_34_out, and_35_out,
       and_36_out, and_37_out, and_38_out, and_39_out, and_40_out, and_41_out, and_42_out, and_43_out,
       and_44_out, and_45_out, and_46_out, and_47_out, and_48_out, and_49_out, and_50_out, and_51_out,
       and_52_out, ET_2_out, ET_3_out, ET_4_out, ET_out, not_1_out, not_2_out, not_3_out, not_4_out,
       not_5_out, not_6_out, not_7_out, not_8_out, not_9_out, not_10_out, not_11_out, not_12_out, or_1_out,
       or_2_out, or_3_out, or_4_out, or_5_out, or_6_out, or_7_out, or_8_out, or_10_out, or_12_out, or_14_out,
       xor_1_out, xor_2_out, xor_3_out, xor_4_out, xor_5_out, xor_6_out, xor_7_out, xor_8_out, xor_9_out,
       xor_10_out, xor_11_out, xor_12_out;

  and and_1 (and_1_out, A, EN_A);
  and and_2 (and_2_out, E, EN_E);
  and and_3 (and_3_out, B, EN_B);
  and and_4 (and_4_out, F, EN_F);
  and and_5 (and_5_out, C, EN_C);
  and and_6 (and_6_out, G, EN_G);
  and and_7 (and_7_out, D, EN_D);
  and and_8 (and_8_out, H, EN_H);
  not not_1 (not_1_out, F0);
  not not_2 (not_2_out, F0);
  and and_9 (and_9_out, not_1_out, and_1_out, not_3_out);
  and and_10 (and_10_out, not_1_out, and_2_out, not_3_out);
  and and_11 (and_11_out, not_1_out, Cin, not_3_out);
  and and_12 (and_12_out, not_2_out, and_1_out, F1);
  and and_13 (and_13_out, not_2_out, and_2_out, F1);
  and and_14 (and_14_out, not_2_out, Cin, F1);
  and and_15 (and_15_out, not_1_out, and_3_out, not_3_out);
  and and_16 (and_16_out, not_1_out, and_4_out, not_3_out);
  and and_17 (and_17_out, not_1_out, or_10_out, not_3_out);
  and and_18 (and_18_out, not_2_out, and_3_out, F1);
  and and_19 (and_19_out, not_2_out, and_4_out, F1);
  and and_20 (and_20_out, not_2_out, or_10_out, F1);
  and and_21 (and_21_out, not_1_out, and_5_out, not_3_out);
  and and_22 (and_22_out, not_1_out, and_6_out, not_3_out);
  and and_23 (and_23_out, not_1_out, or_12_out, not_3_out);
  and and_24 (and_24_out, not_2_out, and_5_out, F1);
  and and_25 (and_25_out, not_2_out, and_6_out, F1);
  and and_26 (and_26_out, not_2_out, or_12_out, F1);
  and and_27 (and_27_out, not_1_out, and_7_out, not_3_out);
  and and_28 (and_28_out, not_1_out, and_8_out, not_3_out);
  and and_29 (and_29_out, not_1_out, or_14_out, not_3_out);
  and and_30 (and_30_out, not_2_out, and_7_out, F1);
  and and_31 (and_31_out, not_2_out, and_8_out, F1);
  and and_32 (and_32_out, not_2_out, or_14_out, F1);
  not not_3 (not_3_out, F1);
  not not_4 (not_4_out, F1);
  xor _1 (_1_out, and_9_out, and_10_out);
  not not_5 (not_5_out, and_12_out);
  not not_6 (not_6_out, and_1_out);
  and ET (ET_out, and_1_out, and_2_out);
  xor _1_2 (_1_2_out, and_15_out, and_16_out);
  not not_7 (not_7_out, and_18_out);
  not not_8 (not_8_out, and_3_out);
  and ET_2 (ET_2_out, and_3_out, and_4_out);
  xor _1_3 (_1_3_out, and_21_out, and_22_out);
  not not_9 (not_9_out, and_24_out);
  not not_10 (not_10_out, and_5_out);
  and ET_3 (ET_3_out, and_5_out, and_6_out);
  xor _1_4 (_1_4_out, and_27_out, and_28_out);
  not not_11 (not_11_out, and_30_out);
  not not_12 (not_12_out, and_7_out);
  and ET_4 (ET_4_out, and_7_out, and_8_out);
  xor xor_1 (xor_1_out, and_12_out, and_13_out);
  and and_33 (and_33_out, ET_out, F0, not_4_out);
  xor xor_2 (xor_2_out, and_18_out, and_19_out);
  and and_34 (and_34_out, ET_2_out, F0, not_4_out);
  xor xor_3 (xor_3_out, and_24_out, and_25_out);
  and and_35 (and_35_out, ET_3_out, F0, not_4_out);
  xor xor_4 (xor_4_out, and_30_out, and_31_out);
  and and_36 (and_36_out, ET_4_out, F0, not_4_out);
  xor xor_5 (xor_5_out, _1_out, and_11_out);
  and and_37 (and_37_out, and_11_out, _1_out);
  and and_38 (and_38_out, and_9_out, and_10_out);
  or or_1 (or_1_out, and_14_out, and_13_out);
  xor xor_6 (xor_6_out, _1_2_out, and_17_out);
  and and_39 (and_39_out, and_17_out, _1_2_out);
  and and_40 (and_40_out, and_15_out, and_16_out);
  or or_2 (or_2_out, and_20_out, and_19_out);
  xor xor_7 (xor_7_out, _1_3_out, and_23_out);
  and and_41 (and_41_out, and_23_out, _1_3_out);
  and and_42 (and_42_out, and_21_out, and_22_out);
  or or_3 (or_3_out, and_26_out, and_25_out);
  xor xor_8 (xor_8_out, _1_4_out, and_29_out);
  and and_43 (and_43_out, and_29_out, _1_4_out);
  and and_44 (and_44_out, and_27_out, and_28_out);
  or or_4 (or_4_out, and_32_out, and_31_out);
  or _1_5 (_1_5_out, and_37_out, and_38_out);
  xor xor_9 (xor_9_out, xor_1_out, and_14_out);
  and and_45 (and_45_out, or_1_out, not_5_out);
  and and_46 (and_46_out, F0, not_6_out, F1);
  or _1_6 (_1_6_out, and_39_out, and_40_out);
  xor xor_10 (xor_10_out, xor_2_out, and_20_out);
  and and_47 (and_47_out, or_2_out, not_7_out);
  and and_48 (and_48_out, F0, not_8_out, F1);
  or _1_7 (_1_7_out, and_41_out, and_42_out);
  xor xor_11 (xor_11_out, xor_3_out, and_26_out);
  and and_49 (and_49_out, or_3_out, not_9_out);
  and and_50 (and_50_out, F0, not_10_out, F1);
  or _1_8 (_1_8_out, and_43_out, and_44_out);
  xor xor_12 (xor_12_out, xor_4_out, and_32_out);
  and and_51 (and_51_out, or_4_out, not_11_out);
  and and_52 (and_52_out, F0, not_12_out, F1);
  or or_5 (or_5_out, and_14_out, and_13_out, and_45_out);
  or or_6 (or_6_out, and_20_out, and_19_out, and_47_out);
  or or_7 (or_7_out, and_26_out, and_25_out, and_49_out);
  or or_8 (or_8_out, and_32_out, and_31_out, and_51_out);
  or or_9 (out_20, xor_5_out, xor_9_out, and_46_out, and_33_out);
  or or_10 (or_10_out, _1_5_out, or_5_out);
  or or_11 (out_21, xor_6_out, xor_10_out, and_48_out, and_34_out);
  or or_12 (or_12_out, _1_6_out, or_6_out);
  or or_13 (out_22, xor_7_out, xor_11_out, and_50_out, and_35_out);
  or or_14 (or_14_out, _1_7_out, or_7_out);
  or or_15 (out_23, xor_8_out, xor_12_out, and_52_out, and_36_out);
  or or_16 (Cout, _1_8_out, or_8_out);

  // Notes on the sheet:
  //   ADDITIONNEUR
  //   SOUSTRACTEUR
  //   ADDITIONNEUR
  //   SOUSTRACTEUR
  //   ADDITIONNEUR
  //   SOUSTRACTEUR
  //   ADDITIONNEUR
  //   SOUSTRACTEUR
  //   NON(A)
  //   NON(A)
  //   NON(A)
  //   NON(A)
endmodule
